# Fritzing sketch current sensor (saved by Fritzing 0.9.10b)

parts:
  Part1 = Current Sensor 5A
  LED1 = LED - 5mm [color="Red (633nm)" current=0.030 package="5 mm [THT]"]
  BAT1 = Battery Holders [package=battery-aaa]
  Part2 = Arduino Uno (Rev3)
  R1 = Resistor [tolerance=±5% power=0.25 resistance=220 package=THT]

nets:
  N1: Part1.1, LED1.anode
  N2: Part1.2, Part1.OUT, Part2.A0, R1.Pin_1
  VCC: Part1.VCC, Part2.5V
  GND: Part1.GND, Part2.GND
  N3: LED1.cathode, BAT1.-
  N4: BAT1.+, R1.Pin_0
